// Logisim project rv32i_single_cycle.circ as structural Verilog
module instruction_fetch (
  input  clock,
  input  reset,
  output [31:0] instruction,
  output [31:0] pc
);

  wire [31:0] adder_1_out;

  Register #(.width(32)) register_1 (.D(adder_1_out), .en(1'b1), .clk(clock), .Q(pc), .clr(reset));
  Adder #(.width(32)) adder_1 (.a(pc), .b(32'h4), .out(adder_1_out));  // open: cin, cout
  RAM #(.asyncread("true"), .dataWidth(32)) RAM1 (
    .addr(pc[9:2]), .we(1'b0), .oe(1'b1), .clk(clock), .dout(instruction));  // open: din
endmodule
