// Logisim project tinyGpu.circ as structural Verilog
module ALU (
  input  [2:0] core_state,
  input  enable,
  input  [7:0] rs,
  input  reset,
  input  [7:0] rt,
  input  decoded_alu_output_mux,
  input  clock,
  input  [1:0] decoded_alu_arithmetic_mux,
  output [7:0] alu_out
);

  wire and_1_out, comparator_2_eq;
  wire [2:0] comparator_1_lt;
  wire [7:0] adder_1_out, divider_1_out, multiplexer_1_out, multiplexer_2_out, multiplier_1_out,
       subtractor_1_out;

  Adder adder_1 (.a(rs), .b(rt), .out(adder_1_out));  // open: cin, cout
  Subtractor subtractor_1 (.a(rs), .b(rt), .out(subtractor_1_out));  // open: bin, bout
  Multiplier multiplier_1 (.a(rs), .b(rt), .out(multiplier_1_out));  // open: cin, cout
  Divider divider_1 (.a(rs), .b(rt), .out(divider_1_out));  // open: upper, rem
  Multiplexer #(.select(2), .width(8)) multiplexer_1 (
    .in0(adder_1_out), .in1(subtractor_1_out), .in2(multiplier_1_out), .in3(divider_1_out),
    .out(multiplexer_1_out), .sel(decoded_alu_arithmetic_mux));
  Comparator comparator_1 (
    .a(multiplexer_1_out), .b({8{1'b0}}), .gt(comparator_1_lt[2]), .eq(comparator_1_lt[1]),
    .lt(comparator_1_lt[0]));
  Comparator #(.mode("unsigned"), .width(3)) comparator_2 (
    .a(core_state), .b(3'b101), .eq(comparator_2_eq));  // open: gt, lt
  and and_1 (and_1_out, comparator_2_eq, enable);
  Multiplexer #(.width(8)) multiplexer_2 (
    .in0(multiplexer_1_out), .in1({{5{1'b0}}, comparator_1_lt}), .out(multiplexer_2_out),
    .sel(decoded_alu_output_mux));
  Register register_1 (.D(multiplexer_2_out), .en(and_1_out), .clk(clock), .Q(alu_out), .clr(reset));
endmodule

module Registers (
  input  [3:0] decoded_rt_address,
  input  [3:0] decoded_rs_address,
  input  reset,
  input  [7:0] blockDim,
  input  [7:0] threadIdx,
  input  [7:0] alu_out,
  input  [7:0] lsu_out,
  input  [7:0] blockId,
  input  [7:0] decoded_immediate,
  input  [1:0] decoded_reg_input_mux,
  input  clock,
  input  enable,
  input  [2:0] core_state,
  input  decoded_reg_write_enable,
  input  [3:0] decoded_rd_address,
  output [7:0] rt_op,
  output [7:0] rs_op
);

  wire and_1_out, and_2_out, and_3_out, and_4_out, and_5_out, and_6_out, and_7_out, and_8_out, and_9_out,
       and_10_out, and_11_out, and_12_out, and_13_out, and_14_out, and_15_out, and_16_out, and_17_out,
       and_18_out, comparator_1_eq, comparator_2_eq, decoder_1_out0, decoder_1_out1, decoder_1_out2,
       decoder_1_out3, decoder_1_out4, decoder_1_out5, decoder_1_out6, decoder_1_out7, decoder_1_out8,
       decoder_1_out9, decoder_1_out10, decoder_1_out11, decoder_1_out12, decoder_1_out13, decoder_1_out14,
       decoder_1_out15;
  wire [7:0] multiplexer_1_out, multiplexer_2_out, multiplexer_3_out, register_1_q, register_2_q,
       register_3_q, register_4_q, register_5_q, register_6_q, register_7_q, register_8_q, register_9_q,
       register_10_q, register_11_q, register_12_q, register_13_q, register_14_q;

  Decoder #(.enable("false"), .select(4)) decoder_1 (
    .out0(decoder_1_out0), .out1(decoder_1_out1), .out2(decoder_1_out2), .out3(decoder_1_out3),
    .out4(decoder_1_out4), .out5(decoder_1_out5), .out6(decoder_1_out6), .out7(decoder_1_out7),
    .out8(decoder_1_out8), .out9(decoder_1_out9), .out10(decoder_1_out10), .out11(decoder_1_out11),
    .out12(decoder_1_out12), .out13(decoder_1_out13), .out14(decoder_1_out14), .out15(decoder_1_out15),
    .sel(decoded_rd_address));
  Multiplexer #(.select(2), .width(8)) multiplexer_1 (
    .in0(alu_out), .in1(lsu_out), .in2(decoded_immediate), .out(multiplexer_1_out),
    .sel(decoded_reg_input_mux));  // open: in3
  and and_1 (and_1_out, enable, comparator_1_eq);
  Comparator #(.mode("unsigned"), .width(3)) comparator_1 (
    .a(3'b011), .b(core_state), .eq(comparator_1_eq));  // open: gt, lt
  Comparator #(.mode("unsigned"), .width(3)) comparator_2 (
    .a(core_state), .b(3'b110), .eq(comparator_2_eq));  // open: gt, lt
  and and_2 (and_2_out, enable, comparator_2_eq);
  and and_3 (and_3_out, decoded_reg_write_enable, and_2_out, decoder_1_out0);
  Register register_1 (.D(multiplexer_1_out), .en(and_3_out), .clk(clock), .Q(register_1_q), .clr(reset));
  Register register_2 (.D(multiplexer_1_out), .en(and_4_out), .clk(clock), .Q(register_2_q), .clr(reset));
  and and_4 (and_4_out, decoded_reg_write_enable, and_2_out, decoder_1_out8);
  and and_5 (and_5_out, decoded_reg_write_enable, and_2_out, decoder_1_out1);
  and and_6 (and_6_out, decoded_reg_write_enable, and_2_out, decoder_1_out9);
  Register register_3 (.D(multiplexer_1_out), .en(and_5_out), .clk(clock), .Q(register_3_q), .clr(reset));
  Register register_4 (.D(multiplexer_1_out), .en(and_6_out), .clk(clock), .Q(register_4_q), .clr(reset));
  and and_7 (and_7_out, decoded_reg_write_enable, and_2_out, decoder_1_out2);
  and and_8 (and_8_out, decoded_reg_write_enable, and_2_out, decoder_1_out10);
  Register register_5 (.D(multiplexer_1_out), .en(and_7_out), .clk(clock), .Q(register_5_q), .clr(reset));
  Register register_6 (.D(multiplexer_1_out), .en(and_8_out), .clk(clock), .Q(register_6_q), .clr(reset));
  and and_9 (and_9_out, decoded_reg_write_enable, and_2_out, decoder_1_out3);
  and and_10 (and_10_out, decoded_reg_write_enable, and_2_out, decoder_1_out11);
  Register register_7 (.D(multiplexer_1_out), .en(and_9_out), .clk(clock), .Q(register_7_q), .clr(reset));
  Register register_8 (.D(multiplexer_1_out), .en(and_10_out), .clk(clock), .Q(register_8_q), .clr(reset));
  and and_11 (and_11_out, decoded_reg_write_enable, and_2_out, decoder_1_out4);
  and and_12 (and_12_out, decoded_reg_write_enable, and_2_out, decoder_1_out12);
  Register register_9 (.D(multiplexer_1_out), .en(and_11_out), .clk(clock), .Q(register_9_q), .clr(reset));
  Register register_10 (.D(multiplexer_1_out), .en(and_12_out), .clk(clock), .Q(register_10_q), .clr(reset));
  and and_13 (and_13_out, decoded_reg_write_enable, and_2_out, decoder_1_out5);
  and and_14 (and_14_out, decoded_reg_write_enable, and_2_out, decoder_1_out13);
  Register register_11 (.D(multiplexer_1_out), .en(and_13_out), .clk(clock), .Q(register_11_q), .clr(reset));
  Register register_12 (.D(blockId), .en(enable), .clk(clock), .Q(register_12_q), .clr(reset));
  and and_15 (and_15_out, decoded_reg_write_enable, and_2_out, decoder_1_out6);
  and and_16 (and_16_out, decoded_reg_write_enable, and_2_out, decoder_1_out14);
  Register register_13 (.D(multiplexer_1_out), .en(and_15_out), .clk(clock), .Q(register_13_q), .clr(reset));
  and and_17 (and_17_out, decoded_reg_write_enable, and_2_out, decoder_1_out7);
  and and_18 (and_18_out, decoded_reg_write_enable, and_2_out, decoder_1_out15);
  Register register_14 (.D(multiplexer_1_out), .en(and_17_out), .clk(clock), .Q(register_14_q), .clr(reset));
  Multiplexer #(.select(4), .width(8)) multiplexer_2 (
    .in0(register_1_q), .in1(register_3_q), .in2(register_5_q), .in3(register_7_q), .in4(register_9_q),
    .in5(register_11_q), .in6(register_13_q), .in7(register_14_q), .in8(register_2_q), .in9(register_4_q),
    .in10(register_6_q), .in11(register_8_q), .in12(register_10_q), .in13(register_12_q), .in14(blockDim),
    .in15(threadIdx), .out(multiplexer_2_out), .sel(decoded_rt_address));
  Multiplexer #(.select(4), .width(8)) multiplexer_3 (
    .in0(register_1_q), .in1(register_3_q), .in2(register_5_q), .in3(register_7_q), .in4(register_9_q),
    .in5(register_11_q), .in6(register_13_q), .in7(register_14_q), .in8(register_2_q), .in9(register_4_q),
    .in10(register_6_q), .in11(register_8_q), .in12(register_10_q), .in13(register_12_q), .in14(blockDim),
    .in15(threadIdx), .out(multiplexer_3_out), .sel(decoded_rs_address));
  Register rt (.D(multiplexer_2_out), .en(and_1_out), .clk(clock), .Q(rt_op), .clr(reset));
  Register rs (.D(multiplexer_3_out), .en(and_1_out), .clk(clock), .Q(rs_op), .clr(reset));
endmodule

module PC (
  input  enable,
  input  [7:0] current_pc,
  input  [7:0] decoded_immediate,
  input  [2:0] decoded_nzp,
  input  [7:0] alu_out,
  input  decoded_pc_mux,
  input  clock,
  input  reset,
  input  [2:0] core_state,
  input  decoded_nzp_write_enable,
  output [7:0] next_pc_op
);

  wire and_1_out, and_2_out, and_4_out, comparator_1_eq, comparator_2_eq, comparator_3_gt;
  wire [2:0] and_3_out, nzp_q;
  wire [7:0] adder_1_out, multiplexer_1_out;

  Comparator #(.mode("unsigned"), .width(3)) comparator_1 (
    .a(core_state), .b(3'b101), .eq(comparator_1_eq));  // open: gt, lt
  and and_1 (and_1_out, enable, comparator_1_eq);
  Comparator #(.mode("unsigned"), .width(3)) comparator_2 (
    .a(core_state), .b(3'b110), .eq(comparator_2_eq));  // open: gt, lt
  and and_2 (and_2_out, comparator_2_eq, enable, decoded_nzp_write_enable);
  Register #(.width(3)) nzp (.D(alu_out[2:0]), .en(and_2_out), .clk(clock), .Q(nzp_q), .clr(reset));
  assign and_3_out = decoded_nzp & nzp_q;  // AND_Gate and_3, 3 bits wide
  Adder adder_1 (.a(current_pc), .b(8'h1), .out(adder_1_out));  // open: cin, cout
  Multiplexer #(.width(8)) multiplexer_1 (
    .in0(adder_1_out), .in1(decoded_immediate), .out(multiplexer_1_out), .sel(and_4_out));
  Comparator #(.mode("unsigned"), .width(3)) comparator_3 (
    .a(and_3_out), .b(3'b000), .gt(comparator_3_gt));  // open: eq, lt
  and and_4 (and_4_out, comparator_3_gt, decoded_pc_mux);
  Register next_pc (.D(multiplexer_1_out), .en(and_1_out), .clk(clock), .Q(next_pc_op), .clr(reset));
endmodule

module DCR (
  input  [7:0] device_control_data,
  input  device_control_write_enable,
  input  clock,
  input  reset,
  output [7:0] thread_count
);

  Register register_1 (
    .D(device_control_data), .en(device_control_write_enable), .clk(clock), .Q(thread_count), .clr(reset));
endmodule

module InstDecode (
  input  [15:0] instruction,
  input  clock,
  input  reset,
  input  [2:0] core_state,
  output [3:0] decoded_rd_address_op,
  output [3:0] decoded_rs_address_op,
  output [3:0] decoded_rt_address_op,
  output [2:0] decoded_nzp_op,
  output [7:0] decoded_immediate_op,
  output decoded_reg_write_enable_op,
  output decoded_mem_read_enable_op,
  output decoded_mem_write_enable_op,
  output decoded_nzp_write_enable_op,
  output [1:0] decoded_reg_input_mux_op,
  output [1:0] decoded_alu_arithmetic_mux_op,
  output decoded_alu_output_mux_op,
  output decoded_pc_mux_op,
  output decoded_ret_op
);

  wire comparator_1_eq, instcontrollogic_1_alu_op_mux, instcontrollogic_1_mem_read,
       instcontrollogic_1_mem_write, instcontrollogic_1_nzp_write, instcontrollogic_1_pc_mux,
       instcontrollogic_1_reg_write, instcontrollogic_1_ret;
  wire [1:0] instcontrollogic_1_alu_arithmetic_mux, instcontrollogic_1_reg_input_mux;

  Comparator #(.mode("unsigned"), .width(3)) comparator_1 (
    .a(core_state), .b(3'b010), .eq(comparator_1_eq));  // open: gt, lt
  Register #(.width(1)) decoded_ret (
    .D(instcontrollogic_1_ret), .en(comparator_1_eq), .clk(clock), .Q(decoded_ret_op), .clr(reset));
  Register #(.width(4)) decoded_rd_address (
    .D(instruction[11:8]), .en(comparator_1_eq), .clk(clock), .Q(decoded_rd_address_op), .clr(reset));
  Register #(.width(1)) decoded_pc_mux (
    .D(instcontrollogic_1_pc_mux), .en(comparator_1_eq), .clk(clock), .Q(decoded_pc_mux_op), .clr(reset));
  Register #(.width(4)) decoded_rs_address (
    .D(instruction[7:4]), .en(comparator_1_eq), .clk(clock), .Q(decoded_rs_address_op), .clr(reset));
  Register #(.width(1)) decoded_alu_output_mux (
    .D(instcontrollogic_1_alu_op_mux), .en(comparator_1_eq), .clk(clock), .Q(decoded_alu_output_mux_op),
    .clr(reset));
  Register #(.width(4)) decoded_rt_address (
    .D(instruction[3:0]), .en(comparator_1_eq), .clk(clock), .Q(decoded_rt_address_op), .clr(reset));
  Register #(.width(2)) decoded_alu_arithmetic_mux (
    .D(instcontrollogic_1_alu_arithmetic_mux), .en(comparator_1_eq), .clk(clock),
    .Q(decoded_alu_arithmetic_mux_op), .clr(reset));
  Register #(.width(3)) decoded_nzp (
    .D(instruction[11:9]), .en(comparator_1_eq), .clk(clock), .Q(decoded_nzp_op), .clr(reset));
  Register #(.width(2)) decoded_reg_input_mux (
    .D(instcontrollogic_1_reg_input_mux), .en(comparator_1_eq), .clk(clock), .Q(decoded_reg_input_mux_op),
    .clr(reset));
  Register decoded_immediate (
    .D(instruction[7:0]), .en(comparator_1_eq), .clk(clock), .Q(decoded_immediate_op), .clr(reset));
  Register #(.width(1)) decoded_nzp_write_enable (
    .D(instcontrollogic_1_nzp_write), .en(comparator_1_eq), .clk(clock), .Q(decoded_nzp_write_enable_op),
    .clr(reset));
  Register #(.width(1)) decoded_reg_write_enable (
    .D(instcontrollogic_1_reg_write), .en(comparator_1_eq), .clk(clock), .Q(decoded_reg_write_enable_op),
    .clr(reset));
  Register #(.width(1)) decoded_mem_write_enable (
    .D(instcontrollogic_1_mem_write), .en(comparator_1_eq), .clk(clock), .Q(decoded_mem_write_enable_op),
    .clr(reset));
  InstControlLogic instcontrollogic_1 (
    .opCode(instruction[15:12]), .pc_mux(instcontrollogic_1_pc_mux),
    .reg_write(instcontrollogic_1_reg_write), .nzp_write(instcontrollogic_1_nzp_write),
    .alu_op_mux(instcontrollogic_1_alu_op_mux), .reg_input_mux(instcontrollogic_1_reg_input_mux),
    .alu_arithmetic_mux(instcontrollogic_1_alu_arithmetic_mux), .mem_read(instcontrollogic_1_mem_read),
    .mem_write(instcontrollogic_1_mem_write), .ret(instcontrollogic_1_ret));
  Register #(.width(1)) decoded_mem_read_enable (
    .D(instcontrollogic_1_mem_read), .en(comparator_1_eq), .clk(clock), .Q(decoded_mem_read_enable_op),
    .clr(reset));
endmodule

module InstControlLogic (
  input  [3:0] opCode,
  output pc_mux,
  output reg_write,
  output nzp_write,
  output alu_op_mux,
  output [1:0] reg_input_mux,
  output [1:0] alu_arithmetic_mux,
  output mem_read,
  output mem_write,
  output ret
);

  wire comparator_3_eq, comparator_4_eq, comparator_5_eq, comparator_6_eq;

  Comparator #(.mode("unsigned"), .width(4)) comparator_1 (.a(opCode), .b(4'b0001), .eq(pc_mux));  // open: gt, lt
  Comparator #(.mode("unsigned"), .width(4)) comparator_2 (.a(opCode), .b(4'b0010), .eq(alu_op_mux));  // open: gt, lt
  Comparator #(.mode("unsigned"), .width(4)) comparator_3 (
    .a(opCode), .b(4'b0011), .eq(comparator_3_eq));  // open: gt, lt
  Comparator #(.mode("unsigned"), .width(4)) comparator_4 (
    .a(opCode), .b(4'b0100), .eq(comparator_4_eq));  // open: gt, lt
  Comparator #(.mode("unsigned"), .width(4)) comparator_5 (
    .a(opCode), .b(4'b0101), .eq(comparator_5_eq));  // open: gt, lt
  Comparator #(.mode("unsigned"), .width(4)) comparator_6 (
    .a(opCode), .b(4'b0110), .eq(comparator_6_eq));  // open: gt, lt
  Comparator #(.mode("unsigned"), .width(4)) comparator_7 (.a(opCode), .b(4'b0111), .eq(mem_read));  // open: gt, lt
  Comparator #(.mode("unsigned"), .width(4)) comparator_8 (.a(opCode), .b(4'b1000), .eq(mem_write));  // open: gt, lt
  Comparator #(.mode("unsigned"), .width(4)) comparator_9 (
    .a(opCode), .b(4'b1001), .eq(reg_input_mux[1]));  // open: gt, lt
  Comparator #(.mode("unsigned"), .width(4)) comparator_10 (.a(opCode), .b(4'b1111), .eq(ret));  // open: gt, lt
  or or_1 (reg_write, comparator_3_eq, comparator_4_eq, comparator_5_eq, comparator_6_eq, mem_read, reg_input_mux[1]);
  or or_2 (alu_arithmetic_mux[0], comparator_4_eq, comparator_6_eq);
  or or_3 (alu_arithmetic_mux[1], comparator_5_eq, comparator_6_eq);

  assign nzp_write = alu_op_mux;
  assign reg_input_mux[0] = mem_read;
endmodule

module Fetcher (
  input  mem_read_ready,
  input  [7:0] current_pc,
  input  [2:0] core_state,
  input  [15:0] mem_read_data,
  input  clock,
  input  reset,
  output mem_read_valid_op,
  output [7:0] mem_read_address_op,
  output [2:0] fetcher_state_op,
  output [15:0] instruction_op
);

  wire and_1_out, and_2_out, and_3_out, and_4_out, and_5_out, comparator_1_eq, comparator_2_eq,
       comparator_3_eq, comparator_4_eq, comparator_5_eq, not_1_out, not_2_out, or_1_out, undriven;
  wire [2:0] multiplexer_4_out, multiplexer_6_out, multiplexer_7_out, multiplexer_8_out;
  wire [7:0] multiplexer_1_out, multiplexer_3_out;
  wire [15:0] multiplexer_2_out, multiplexer_5_out;

  Comparator #(.mode("unsigned"), .width(3)) comparator_1 (
    .a(3'b001), .b(fetcher_state_op), .eq(comparator_1_eq));  // open: gt, lt
  Comparator #(.mode("unsigned"), .width(3)) comparator_2 (
    .a(3'b000), .b(fetcher_state_op), .eq(comparator_2_eq));  // open: gt, lt
  Comparator #(.mode("unsigned"), .width(3)) comparator_3 (
    .a(3'b001), .b(core_state), .eq(comparator_3_eq));  // open: gt, lt
  Comparator #(.mode("unsigned"), .width(3)) comparator_4 (
    .a(3'b010), .b(fetcher_state_op), .eq(comparator_4_eq));  // open: gt, lt
  Comparator #(.mode("unsigned"), .width(3)) comparator_5 (
    .a(3'b010), .b(core_state), .eq(comparator_5_eq));  // open: gt, lt
  not not_1 (not_1_out, and_1_out);
  and and_1 (and_1_out, mem_read_ready, comparator_1_eq);
  and and_2 (and_2_out, comparator_2_eq, comparator_3_eq);
  and and_3 (and_3_out, comparator_4_eq, comparator_5_eq);
  and and_4 (and_4_out, mem_read_valid_op, not_1_out);
  or or_1 (or_1_out, and_4_out, and_2_out);
  Multiplexer #(.width(8)) multiplexer_1 (
    .in0(mem_read_address_op), .in1(current_pc), .out(multiplexer_1_out), .sel(and_2_out));
  Multiplexer #(.width(16)) multiplexer_2 (
    .in0(instruction_op), .in1(mem_read_data), .out(multiplexer_2_out), .sel(and_1_out));
  not not_2 (not_2_out, reset);
  Multiplexer #(.width(8)) multiplexer_3 (
    .in0(multiplexer_1_out), .in1({8{1'b0}}), .out(multiplexer_3_out), .sel(reset));
  Multiplexer #(.width(3)) multiplexer_4 (
    .in0(fetcher_state_op), .in1(3'b001), .out(multiplexer_4_out), .sel(and_2_out));
  Multiplexer #(.width(16)) multiplexer_5 (
    .in0(multiplexer_2_out), .in1({16{1'b0}}), .out(multiplexer_5_out), .sel(reset));
  Register #(.width(1)) mem_read_valid (.D(and_5_out), .en(1'b1), .clk(clock), .Q(mem_read_valid_op));  // open: clr
  and and_5 (and_5_out, or_1_out, not_2_out);
  Register mem_read_address (.D(multiplexer_3_out), .en(1'b1), .clk(clock), .Q(mem_read_address_op));  // open: clr
  Multiplexer #(.width(3)) multiplexer_6 (
    .in0(multiplexer_4_out), .in1(3'b010), .out(multiplexer_6_out), .sel(and_1_out));
  Register #(.width(16)) instruction (.D(multiplexer_5_out), .en(1'b1), .clk(clock), .Q(instruction_op));  // open: clr
  Multiplexer #(.width(3)) multiplexer_7 (
    .in0(multiplexer_6_out), .in1(3'b000), .out(multiplexer_7_out), .sel(and_3_out));
  Register #(.width(3)) fetcher_state (
    .D(multiplexer_8_out), .en(1'b1), .clk(clock), .Q(fetcher_state_op), .clr(undriven));
  Multiplexer #(.width(3)) multiplexer_8 (.in0(multiplexer_7_out), .in1(3'b000), .out(multiplexer_8_out), .sel(reset));
endmodule

module LSU (
  input  [7:0] rs,
  input  [7:0] mem_read_data,
  input  enable,
  input  decoded_mem_read_enable,
  input  [7:0] rt,
  input  decoded_mem_write_enable,
  input  mem_read_ready,
  input  mem_write_ready,
  input  clock,
  input  [2:0] core_state,
  input  reset,
  output mem_read_valid_op,
  output [7:0] mem_read_address_op,
  output [7:0] lsu_out_op,
  output mem_write_valid_op,
  output [7:0] mem_write_address_op,
  output [7:0] mem_write_data_op,
  output [1:0] lsu_state_op
);

  wire LSUState1_is_idle, LSUState1_is_requesting, LSUState1_is_waiting;

  LSURead LSURead1 (
    .rs(rs), .mem_read_data(mem_read_data), .enable(enable),
    .decoded_mem_read_enable(decoded_mem_read_enable), .mem_read_ready(mem_read_ready),
    .is_idle(LSUState1_is_idle), .core_state(core_state), .is_waiting(LSUState1_is_waiting), .clock(clock),
    .reset(reset), .m_rd_valid_op(mem_read_valid_op), .m_rd_addr_op(mem_read_address_op),
    .lsu_out_op(lsu_out_op));
  LSUState LSUState1 (
    .d_m_r_en(decoded_mem_read_enable), .d_m_w_en(decoded_mem_write_enable), .mem_read_ready(mem_read_ready),
    .mem_write_ready(mem_write_ready), .reset(reset), .enable(enable), .clock(clock),
    .core_state(core_state), .is_idle(LSUState1_is_idle), .lsu_state_op(lsu_state_op),
    .is_requesting(LSUState1_is_requesting), .is_waiting(LSUState1_is_waiting));  // open: is_done
  LSUWrite LSUWrite1 (
    .enable(enable), .is_requesting(LSUState1_is_requesting),
    .decoded_mem_write_enable(decoded_mem_write_enable), .is_waiting(LSUState1_is_waiting),
    .mem_write_ready(mem_write_ready), .rs(rs), .rt(rt), .clock(clock), .core_state(core_state),
    .reset(reset), .m_wr_va_op(mem_write_valid_op), .m_wr_addr_op(mem_write_address_op),
    .m_wr_data_op(mem_write_data_op));
endmodule

module LSUState (
  input  d_m_r_en,
  input  d_m_w_en,
  input  mem_read_ready,
  input  mem_write_ready,
  input  reset,
  input  enable,
  input  clock,
  input  [2:0] core_state,
  output is_idle,
  output [1:0] lsu_state_op,
  output is_requesting,
  output is_waiting,
  output is_done
);

  wire and_1_out, and_2_out, and_3_out, and_4_out, and_5_out, comparator_1_eq, comparator_2_eq, or_1_out,
       or_2_out, or_3_out;
  wire [1:0] multiplexer_1_out, multiplexer_2_out, multiplexer_3_out, multiplexer_4_out, multiplexer_5_out;

  or or_1 (or_1_out, d_m_r_en, d_m_w_en);
  Comparator #(.mode("unsigned"), .width(3)) comparator_1 (
    .a(core_state), .b(3'b011), .eq(comparator_1_eq));  // open: gt, lt
  Comparator #(.mode("unsigned"), .width(3)) comparator_2 (
    .a(core_state), .b(3'b110), .eq(comparator_2_eq));  // open: gt, lt
  Comparator #(.mode("unsigned"), .width(2)) comparator_3 (.a(lsu_state_op), .b(2'b00), .eq(is_idle));  // open: gt, lt
  Comparator #(.mode("unsigned"), .width(2)) comparator_4 (
    .a(lsu_state_op), .b(2'b01), .eq(is_requesting));  // open: gt, lt
  Comparator #(.mode("unsigned"), .width(2)) comparator_5 (
    .a(lsu_state_op), .b(2'b10), .eq(is_waiting));  // open: gt, lt
  Comparator #(.mode("unsigned"), .width(2)) comparator_6 (.a(lsu_state_op), .b(2'b11), .eq(is_done));  // open: gt, lt
  and and_1 (and_1_out, is_idle, comparator_1_eq, or_1_out);
  and and_2 (and_2_out, is_waiting, d_m_r_en, mem_read_ready);
  and and_3 (and_3_out, is_waiting, d_m_w_en, mem_write_ready);
  Multiplexer #(.width(2)) multiplexer_1 (.in0(lsu_state_op), .in1(2'b01), .out(multiplexer_1_out), .sel(and_1_out));
  Multiplexer #(.width(2)) multiplexer_2 (
    .in0(multiplexer_1_out), .in1(2'b10), .out(multiplexer_2_out), .sel(and_4_out));
  and and_4 (and_4_out, or_1_out, is_requesting);
  or or_2 (or_2_out, and_2_out, and_3_out);
  Multiplexer #(.width(2)) multiplexer_3 (
    .in0(multiplexer_2_out), .in1(2'b11), .out(multiplexer_3_out), .sel(or_2_out));
  Multiplexer #(.width(2)) multiplexer_4 (
    .in0(multiplexer_3_out), .in1(2'b00), .out(multiplexer_4_out), .sel(and_5_out));
  and and_5 (and_5_out, is_done, comparator_2_eq, or_1_out);
  Multiplexer #(.width(2)) multiplexer_5 (.in0(multiplexer_4_out), .in1(2'b00), .out(multiplexer_5_out), .sel(reset));
  or or_3 (or_3_out, reset, enable);
  Register #(.width(2)) lsu_state (.D(multiplexer_5_out), .en(or_3_out), .clk(clock), .Q(lsu_state_op));  // open: clr
endmodule

module LSURead (
  input  [7:0] rs,
  input  [7:0] mem_read_data,
  input  enable,
  input  decoded_mem_read_enable,
  input  mem_read_ready,
  input  is_idle,
  input  [2:0] core_state,
  input  is_waiting,
  input  clock,
  input  reset,
  output m_rd_valid_op,
  output [7:0] m_rd_addr_op,
  output [7:0] lsu_out_op
);

  wire and_1_out, and_2_out, comparator_1_eq, multiplexer_1_out, multiplexer_2_out, multiplexer_3_out,
       or_1_out;
  wire [7:0] multiplexer_4_out, multiplexer_5_out, multiplexer_6_out, multiplexer_7_out;

  Multiplexer multiplexer_1 (.in0(m_rd_valid_op), .in1(1'b0), .out(multiplexer_1_out), .sel(and_1_out));
  and and_1 (and_1_out, is_waiting, decoded_mem_read_enable, mem_read_ready);
  Comparator #(.mode("unsigned"), .width(3)) comparator_1 (
    .a(core_state), .b(3'b011), .eq(comparator_1_eq));  // open: gt, lt
  and and_2 (and_2_out, is_idle, comparator_1_eq, decoded_mem_read_enable);
  Multiplexer multiplexer_2 (.in0(multiplexer_1_out), .in1(1'b1), .out(multiplexer_2_out), .sel(and_2_out));
  Multiplexer multiplexer_3 (.in0(multiplexer_2_out), .in1(1'b0), .out(multiplexer_3_out), .sel(reset));
  Register #(.width(1)) mem_read_valid (
    .D(multiplexer_3_out), .en(or_1_out), .clk(clock), .Q(m_rd_valid_op));  // open: clr
  or or_1 (or_1_out, enable, reset);
  Multiplexer #(.width(8)) multiplexer_4 (.in0(m_rd_addr_op), .in1(rs), .out(multiplexer_4_out), .sel(and_2_out));
  Multiplexer #(.width(8)) multiplexer_5 (
    .in0(lsu_out_op), .in1(mem_read_data), .out(multiplexer_5_out), .sel(and_1_out));
  Register mem_read_address (.D(multiplexer_6_out), .en(or_1_out), .clk(clock), .Q(m_rd_addr_op));  // open: clr
  Multiplexer #(.width(8)) multiplexer_6 (
    .in0(multiplexer_4_out), .in1({8{1'b0}}), .out(multiplexer_6_out), .sel(reset));
  Multiplexer #(.width(8)) multiplexer_7 (
    .in0(multiplexer_5_out), .in1({8{1'b0}}), .out(multiplexer_7_out), .sel(reset));
  Register lsu_out (.D(multiplexer_7_out), .en(or_1_out), .clk(clock), .Q(lsu_out_op));  // open: clr
endmodule

module LSUWrite (
  input  enable,
  input  is_requesting,
  input  decoded_mem_write_enable,
  input  is_waiting,
  input  mem_write_ready,
  input  [7:0] rs,
  input  [7:0] rt,
  input  clock,
  input  [2:0] core_state,
  input  reset,
  output m_wr_va_op,
  output [7:0] m_wr_addr_op,
  output [7:0] m_wr_data_op
);

  wire and_1_out, and_2_out, multiplexer_1_out, multiplexer_4_out, multiplexer_5_out;
  wire [7:0] multiplexer_2_out, multiplexer_3_out, multiplexer_6_out, multiplexer_7_out;

  and and_1 (and_1_out, enable, is_requesting, decoded_mem_write_enable);
  and and_2 (and_2_out, enable, decoded_mem_write_enable, is_waiting, mem_write_ready);
  Multiplexer multiplexer_1 (.in0(m_wr_va_op), .in1(1'b1), .out(multiplexer_1_out), .sel(and_1_out));
  Multiplexer #(.width(8)) multiplexer_2 (.in0(m_wr_addr_op), .in1(rs), .out(multiplexer_2_out), .sel(and_1_out));
  Multiplexer #(.width(8)) multiplexer_3 (.in0(m_wr_data_op), .in1(rt), .out(multiplexer_3_out), .sel(and_1_out));
  Multiplexer multiplexer_4 (.in0(multiplexer_1_out), .in1(1'b0), .out(multiplexer_4_out), .sel(and_2_out));
  Multiplexer multiplexer_5 (.in0(multiplexer_4_out), .in1(1'b0), .out(multiplexer_5_out), .sel(reset));
  Register mem_write_address (.D(multiplexer_6_out), .en(1'b1), .clk(clock), .Q(m_wr_addr_op));  // open: clr
  Multiplexer #(.width(8)) multiplexer_6 (
    .in0(multiplexer_2_out), .in1({8{1'b0}}), .out(multiplexer_6_out), .sel(reset));
  Register mem_write_data (.D(multiplexer_7_out), .en(1'b1), .clk(clock), .Q(m_wr_data_op));  // open: clr
  Multiplexer #(.width(8)) multiplexer_7 (
    .in0(multiplexer_3_out), .in1({8{1'b0}}), .out(multiplexer_7_out), .sel(reset));
  Register #(.width(1)) mem_write_valid (.D(multiplexer_5_out), .en(1'b1), .clk(clock), .Q(m_wr_va_op));  // open: clr
endmodule

module SchedulerState (
  input  decoded_ret,
  input  [1:0] lsu_state_0,
  input  [1:0] lsu_state_1,
  input  [1:0] lsu_state_2,
  input  [1:0] lsu_state_3,
  input  [2:0] fetcher_state,
  input  [7:0] next_pc_3,
  input  start,
  input  clock,
  input  reset,
  output done_op,
  output [2:0] core_state_op,
  output [7:0] current_pc_op
);

  wire and_1_out, and_2_out, and_3_out, and_4_out, and_5_out, AnyLSUWaiting1_any_lsu_waiting_op,
       comparator_1_eq, comparator_2_eq, comparator_3_eq, comparator_4_eq, comparator_5_eq, comparator_6_eq,
       comparator_7_eq, comparator_8_eq, multiplexer_9_out, multiplexer_11_out, not_1_out, not_2_out;
  wire [2:0] multiplexer_1_out, multiplexer_2_out, multiplexer_3_out, multiplexer_4_out, multiplexer_5_out,
       multiplexer_6_out, multiplexer_7_out, multiplexer_8_out, multiplexer_10_out;
  wire [7:0] multiplexer_12_out, multiplexer_13_out;

  not not_1 (not_1_out, decoded_ret);
  Comparator #(.mode("unsigned"), .width(3)) comparator_1 (
    .a(3'b110), .b(core_state_op), .eq(comparator_1_eq));  // open: gt, lt
  Multiplexer #(.width(3)) multiplexer_1 (.in0(core_state_op), .in1(3'b001), .out(multiplexer_1_out), .sel(and_1_out));
  and and_1 (and_1_out, not_1_out, comparator_1_eq);
  and and_2 (and_2_out, decoded_ret, comparator_1_eq);
  Multiplexer #(.width(3)) multiplexer_2 (
    .in0(multiplexer_1_out), .in1(3'b111), .out(multiplexer_2_out), .sel(and_2_out));
  Comparator #(.mode("unsigned"), .width(3)) comparator_2 (
    .a(3'b101), .b(core_state_op), .eq(comparator_2_eq));  // open: gt, lt
  AnyLSUWaiting AnyLSUWaiting1 (
    .lsu_state_0(lsu_state_0), .lsu_state_1(lsu_state_1), .lsu_state_2(lsu_state_2),
    .lsu_state_3(lsu_state_3), .any_lsu_waiting_op(AnyLSUWaiting1_any_lsu_waiting_op));
  Multiplexer #(.width(3)) multiplexer_3 (
    .in0(multiplexer_2_out), .in1(3'b110), .out(multiplexer_3_out), .sel(comparator_2_eq));
  Comparator #(.mode("unsigned"), .width(3)) comparator_3 (
    .a(3'b100), .b(core_state_op), .eq(comparator_3_eq));  // open: gt, lt
  not not_2 (not_2_out, AnyLSUWaiting1_any_lsu_waiting_op);
  Multiplexer #(.width(3)) multiplexer_4 (
    .in0(multiplexer_3_out), .in1(3'b101), .out(multiplexer_4_out), .sel(and_3_out));
  and and_3 (and_3_out, comparator_3_eq, not_2_out);
  Comparator #(.mode("unsigned"), .width(3)) comparator_4 (
    .a(3'b011), .b(core_state_op), .eq(comparator_4_eq));  // open: gt, lt
  Multiplexer #(.width(3)) multiplexer_5 (
    .in0(multiplexer_4_out), .in1(3'b100), .out(multiplexer_5_out), .sel(comparator_4_eq));
  Comparator #(.mode("unsigned"), .width(3)) comparator_5 (
    .a(3'b010), .b(core_state_op), .eq(comparator_5_eq));  // open: gt, lt
  Comparator #(.mode("unsigned"), .width(3)) comparator_6 (
    .a(core_state_op), .b(3'b001), .eq(comparator_6_eq));  // open: gt, lt
  Comparator #(.mode("unsigned"), .width(3)) comparator_7 (
    .a(fetcher_state), .b(3'b010), .eq(comparator_7_eq));  // open: gt, lt
  Multiplexer #(.width(3)) multiplexer_6 (
    .in0(multiplexer_5_out), .in1(3'b011), .out(multiplexer_6_out), .sel(comparator_5_eq));
  and and_4 (and_4_out, comparator_6_eq, comparator_7_eq);
  Comparator #(.mode("unsigned"), .width(3)) comparator_8 (
    .a(core_state_op), .b(3'b000), .eq(comparator_8_eq));  // open: gt, lt
  Multiplexer #(.width(3)) multiplexer_7 (
    .in0(multiplexer_6_out), .in1(3'b010), .out(multiplexer_7_out), .sel(and_4_out));
  and and_5 (and_5_out, comparator_8_eq, start);
  Multiplexer #(.width(3)) multiplexer_8 (
    .in0(multiplexer_7_out), .in1(3'b001), .out(multiplexer_8_out), .sel(and_5_out));
  Multiplexer multiplexer_9 (.in0(done_op), .in1(1'b1), .out(multiplexer_9_out), .sel(and_2_out));
  Register #(.width(3)) core_state (.D(multiplexer_10_out), .en(1'b1), .clk(clock), .Q(core_state_op));  // open: clr
  Multiplexer #(.width(3)) multiplexer_10 (
    .in0(multiplexer_8_out), .in1(3'b000), .out(multiplexer_10_out), .sel(reset));
  Register #(.width(1)) done (.D(multiplexer_11_out), .en(1'b1), .clk(clock), .Q(done_op));  // open: clr
  Multiplexer multiplexer_11 (.in0(multiplexer_9_out), .in1(1'b0), .out(multiplexer_11_out), .sel(reset));
  Multiplexer #(.width(8)) multiplexer_12 (
    .in0(current_pc_op), .in1(next_pc_3), .out(multiplexer_12_out), .sel(and_1_out));
  Register current_pc (.D(multiplexer_13_out), .en(1'b1), .clk(clock), .Q(current_pc_op));  // open: clr
  Multiplexer #(.width(8)) multiplexer_13 (
    .in0(multiplexer_12_out), .in1({8{1'b0}}), .out(multiplexer_13_out), .sel(reset));
endmodule

module AnyLSUWaiting (
  input  [1:0] lsu_state_0,
  input  [1:0] lsu_state_1,
  input  [1:0] lsu_state_2,
  input  [1:0] lsu_state_3,
  output any_lsu_waiting_op
);

  wire comparator_1_eq, comparator_2_eq, comparator_3_eq, comparator_4_eq, comparator_5_eq, comparator_6_eq,
       comparator_7_eq, comparator_8_eq, or_1_out, or_2_out, or_3_out, or_4_out;

  Comparator #(.mode("unsigned"), .width(2)) comparator_1 (
    .a(2'b01), .b(lsu_state_0), .eq(comparator_1_eq));  // open: gt, lt
  Comparator #(.mode("unsigned"), .width(2)) comparator_2 (
    .a(lsu_state_0), .b(2'b10), .eq(comparator_2_eq));  // open: gt, lt
  Comparator #(.mode("unsigned"), .width(2)) comparator_3 (
    .a(2'b01), .b(lsu_state_1), .eq(comparator_3_eq));  // open: gt, lt
  Comparator #(.mode("unsigned"), .width(2)) comparator_4 (
    .a(lsu_state_1), .b(2'b10), .eq(comparator_4_eq));  // open: gt, lt
  Comparator #(.mode("unsigned"), .width(2)) comparator_5 (
    .a(2'b01), .b(lsu_state_2), .eq(comparator_5_eq));  // open: gt, lt
  Comparator #(.mode("unsigned"), .width(2)) comparator_6 (
    .a(lsu_state_2), .b(2'b10), .eq(comparator_6_eq));  // open: gt, lt
  Comparator #(.mode("unsigned"), .width(2)) comparator_7 (
    .a(2'b01), .b(lsu_state_3), .eq(comparator_7_eq));  // open: gt, lt
  Comparator #(.mode("unsigned"), .width(2)) comparator_8 (
    .a(lsu_state_3), .b(2'b10), .eq(comparator_8_eq));  // open: gt, lt
  or or_1 (or_1_out, comparator_1_eq, comparator_2_eq);
  or or_2 (or_2_out, comparator_3_eq, comparator_4_eq);
  or or_3 (or_3_out, comparator_5_eq, comparator_6_eq);
  or or_4 (or_4_out, comparator_7_eq, comparator_8_eq);
  or or_5 (any_lsu_waiting_op, or_1_out, or_2_out, or_3_out, or_4_out);
endmodule
